// Logisim project 00_nor_gate.circ as structural Verilog: 2 circuits, main circuit main
module main (
  input  in_1,
  input  in_2,
  output out_3
);

  NOR nor_1 (.A(in_1), .B(in_2), .O(out_3));
endmodule

module NOR (
  input  A,
  input  B,
  output O
);

  Pull_Resistor #(.pull(1)) pull_resistor_1 (.node(O));
  Transistor #(.\type ("n")) transistor_1 (.in(1'b0), .out(O), .gate(A));
  Transistor #(.\type ("n")) transistor_2 (.in(1'b0), .out(O), .gate(B));
endmodule
